# Fritzing sketch laser_harp_A4988 (saved by Fritzing 1.0.4)

parts:
  Part1 = Arduino Leonardo (Rev3b)
  Part2 = Arduino Uno (Rev3) - ICSP
  R1 = PHOTOCELL [package=photocell]
  R5 = PHOTOCELL [package=photocell]
  R3 = PHOTOCELL [package=photocell]
  R4 = PHOTOCELL [package=photocell]
  R6 = Resistor [tolerance=±5% resistance=10k package="1206 [SMD]"]
  R7 = Resistor [tolerance=±5% resistance=10k package="1206 [SMD]"]
  R8 = Resistor [tolerance=±5% resistance=10k package="1206 [SMD]"]
  R9 = Resistor [tolerance=±5% resistance=10k package="1206 [SMD]"]
  V1 = DC Power [voltage=12V]
  Laser = IC, DIP package, 8 pins [chip_label="RGB Laser"]
  IC1 = IC, DIP package, 6 pins [chip_label=Relay]
  IC2 = IC, SIP package, 4 pins [chip_label=TCRT5000]
  SEN1 = US-100 Ultrasonic Distance Sensor
  SEN2 = US-100 Ultrasonic Distance Sensor
  Pololu_A1 = Pololu A4988 [package=SO16]
  M2 = Stepper Motor - Bipolar
  part = Electrolytic Capacitor [capacitance=100μF voltage=35V package="0807 [SMD, electrolytic]"]

nets:
  N1: Part1.D0/RX, SEN2.ECHO
  N2: Part1.D1/TX, SEN2.TRIG
  N3: Part1.D3_PWM/SCL, Part1.SCL, Part2.A5/SCL
  VCC: Part1.5V, R1.P$1, R5.P$1, R3.P$1, R4.P$2, SEN1.VCC, SEN2.VCC
  GND: Part1.GND, Part2.GND, R6.Pin_1, R7.Pin_1, R8.Pin_1, R9.Pin_1, Laser.pin4, Laser.pin5, Laser.pin7, IC1.pin2, IC2.pin2, SEN1.GND, SEN1.GND-2, SEN2.GND, SEN2.GND-2, Pololu_A1.GND#8
  N4: Part1.D8/A8, SEN1.TRIG
  N5: Part1.D9_PWM/A9, SEN1.ECHO
  N6: Part1.SDA, Part2.ICSP_MISO, Part2.D12/MISO
  N7: Part2.A0, R1.P$2, R9.Pin_0
  N8: Part2.A1, R5.P$2, R6.Pin_0
  N9: Part2.A2, R3.P$2, R7.Pin_0
  N10: Part2.A3, R4.P$1, R8.Pin_0
  5V: Part2.5V, IC1.pin1, Pololu_A1.VDD
  N11: Part2.D8, Pololu_A1.STEP
  N12: Part2.D9_PWM, Pololu_A1.DIR
  N13: Part2.D2, Laser.pin8
  N14: Part2.D3_PWM, Laser.pin3
  N15: Part2.D4, Laser.pin6
  N16: Part2.D5_PWM, IC1.pin3
  N17: Part2.D6_PWM, IC2.pin3
  N18: Part2.D7, IC2.pin1
  N19: V1.V+, IC1.pin5, Pololu_A1.VMOT, part.+
  N20: V1.V-, Laser.pin2, Pololu_A1.GND#14, part.-
  N21: Laser.pin1, IC1.pin6
  N22: Pololu_A1.RESET, Pololu_A1.SLEEP
  N23: Pololu_A1.1B, M2.D
  N24: Pololu_A1.1A, M2.B
  N25: Pololu_A1.2A, M2.C
  N26: Pololu_A1.2B, M2.A
