# Fritzing sketch laser_harp_ULN2003 (saved by Fritzing 1.0.4)

parts:
  Part1 = Arduino Leonardo (Rev3b)
  Part2 = Arduino Uno (Rev3) - ICSP
  R1 = PHOTOCELL [package=photocell]
  R5 = PHOTOCELL [package=photocell]
  R3 = PHOTOCELL [package=photocell]
  R4 = PHOTOCELL [package=photocell]
  R6 = Resistor [tolerance=±5% resistance=10k package="1206 [SMD]"]
  R7 = Resistor [tolerance=±5% resistance=10k package="1206 [SMD]"]
  R8 = Resistor [tolerance=±5% resistance=10k package="1206 [SMD]"]
  R9 = Resistor [tolerance=±5% resistance=10k package="1206 [SMD]"]
  SM1 = 28BYJ-48 Stepper Motor [part_number=28BYJ-48]
  Driver1 = 28BYJ-48 Driver Module [part_number=ULN2003 package=THT]
  V1 = DC Power [voltage=12V]
  Laser = IC, DIP package, 8 pins [chip_label="RGB Laser"]
  IC1 = IC, DIP package, 6 pins [chip_label=Relay]
  IC2 = IC, SIP package, 4 pins [chip_label=TCRT5000]
  SEN1 = US-100 Ultrasonic Distance Sensor
  SEN2 = US-100 Ultrasonic Distance Sensor

nets:
  N1: Part1.D0/RX, SEN2.ECHO
  N2: Part1.D1/TX, SEN2.TRIG
  N3: Part1.D3_PWM/SCL, Part1.SCL, Part2.A5/SCL
  VCC: Part1.5V, R1.P$1, R5.P$1, R3.P$1, R4.P$2, SEN1.VCC, SEN2.VCC
  GND: Part1.GND, Part2.GND, R6.Pin_1, R7.Pin_1, R8.Pin_1, R9.Pin_1, Laser.pin4, Laser.pin5, Laser.pin7, IC1.pin2, IC2.pin2, SEN1.GND, SEN1.GND-2, SEN2.GND, SEN2.GND-2
  N4: Part1.D8/A8, SEN1.TRIG
  N5: Part1.D9_PWM/A9, SEN1.ECHO
  N6: Part1.SDA, Part2.ICSP_MISO, Part2.D12/MISO
  N7: Part2.A0, R1.P$2, R9.Pin_0
  N8: Part2.A1, R5.P$2, R6.Pin_0
  N9: Part2.A2, R3.P$2, R7.Pin_0
  N10: Part2.A3, R4.P$1, R8.Pin_0
  N11: Part2.5V, IC1.pin1
  N12: Part2.ICSP_MOSI, Part2.D11_PWM/MOSI, Driver1.IN1
  N13: Part2.D8, Driver1.IN4
  N14: Part2.D9_PWM, Driver1.IN3
  N15: Part2.D10_PWM/SS, Driver1.IN2
  N16: Part2.D2, Laser.pin8
  N17: Part2.D3_PWM, Laser.pin3
  N18: Part2.D4, Laser.pin6
  N19: Part2.D5_PWM, IC1.pin3
  N20: Part2.D6_PWM, IC2.pin3
  N21: Part2.D7, IC2.pin1
  N22: SM1.blue-pin, Driver1.blue-pin
  N23: SM1.pink-pin, Driver1.pink-pin
  N24: SM1.yellow-pin, Driver1.yellow-pin
  N25: SM1.orange-pin, Driver1.orange-pin
  N26: SM1.red-pin, Driver1.red-pin
  N27: Driver1.GND, V1.V-, Laser.pin2
  N28: Driver1.Vmotor, V1.V+, IC1.pin5
  N29: Laser.pin1, IC1.pin6

custom parts:
  28BYJ-48 Stepper Motor: Unipolar Stepper Motor 28BYJ-48 Top coil - pink & orange Bottom coil - blue & yellow Common rail - red Connector pins: blue - pink - yellow - orange - red
  28BYJ-48 Driver Module: ULN2003 Driver Module for the 28BYJ-48 Unipolar Stepper Motor LED A - Blue wire - Bottom coil left LED B - Pink wire - Top coil left LED C - Yellow wire - Bottom coil right LED D - Orange wire - Top coil right Common rail - red Connector pins: blue - pink - yellow - orange - red Control pins - IN1 to IN4 Power pins - GND & Vmotor (5-12V) On/Off jumper (if removed, power to motor is cut).
